// Logisim project wiring.circ as structural Verilog: 4 circuits, main circuit splitter-examples
module splitter_examples (
  input  [2:0] in_1,
  input  in_2,
  output out_3,
  output out_4,
  output out_5,
  output out_6,
  output [3:0] alternatingBits,
  output [3:0] bottomHalf
);

  wire clock_1_out, clock_2_out;
  wire [1:0] joystick_1_x, joystick_1_y;
  wire [3:0] slider_1_out;
  wire [7:0] dipswitch_1_sw8;
  wire [7:5] callout_9_p2;
  wire [11:0] counter_1_q;

  // Callout #(.background("#81e6df80"), .dx(48), .dy(23), .foreground("#2e5c56"), .format("wrapped"), .text("join eight signals into one 8-bit bus"), .textwidth(117), .valign("bottom-overall")) callout_1: pin names not known
  DipSwitch dipswitch_1 (
    .sw1(dipswitch_1_sw8[7]), .sw2(dipswitch_1_sw8[6]), .sw3(dipswitch_1_sw8[5]), .sw4(dipswitch_1_sw8[4]),
    .sw5(dipswitch_1_sw8[3]), .sw6(dipswitch_1_sw8[2]), .sw7(dipswitch_1_sw8[1]), .sw8(dipswitch_1_sw8[0]));
  // Probe on slider_1_out
  Slider #(.width(4)) slider_1 (.out(slider_1_out));
  Joystick #(.bits(2)) joystick_1 (.x(joystick_1_x), .y(joystick_1_y));
  // Callout #(.background("#81e6df80"), .dx(12), .dy(-12), .foreground("#2e5c56"), .format("wrapped"), .halign("right"), .text("combined end"), .textwidth(68), .valign("top")) callout_2: pin names not known
  // Probe on joystick_1_x
  // Probe on joystick_1_y
  // Callout #(.background("#81e6df80"), .dx(-22), .dy(-14), .foreground("#2e5c56"), .format("wrapped"), .text("taps"), .textwidth(37), .valign("top")) callout_3: pin names not known
  // Callout #(.background("#81e6df00"), .dx(-20), .dy(8), .foreground("#2e5c56"), .format("wrapped"), .text(""), .textwidth(37), .valign("top")) callout_4: pin names not known
  // Callout #(.background("#81e6df00"), .dx(-18), .dy(39), .foreground("#2e5c56"), .format("wrapped"), .text(""), .textwidth(37), .valign("top")) callout_5: pin names not known
  // Callout #(.background("#81e6df80"), .dx(-29), .dy(21), .foreground("#2e5c56"), .format("wrapped"), .halign("right"), .text("split 8-bit bus into two 4-bit buses"), .textwidth(123), .valign("bottom-overall")) callout_6: pin names not known
  // Callout #(.background("#81e6df80"), .dx(19), .dy(18), .foreground("#2e5c56"), .format("wrapped"), .text("split 4-bit bus into four signals"), .textwidth(123), .valign("bottom-overall")) callout_7: pin names not known
  Adder #(.width(4)) adder_1 (
    .a(dipswitch_1_sw8[3:0]), .b(dipswitch_1_sw8[7:4]), .out({out_6, out_5, out_4, out_3}));  // open: cin, cout
  // Callout #(.background("#81e6df80"), .dx(-25), .dy(-29), .foreground("#2e5c56"), .format("wrapped"), .text("merge a motley set of buses and signals into one 12-bit bus"), .textwidth(123), .valign("bottom-overall")) callout_8: pin names not known
  DotMatrix #(.inputtype("row"), .matrixcols(12), .matrixrows(1)) dotmatrix_1 (.row0({in_2, in_1, joystick_1_y, joystick_1_x, slider_1_out}));
  Random random_1 ();  // open: clk, next, out, clr
  Counter #(.max('hfff), .width(12)) counter_1 (
    .Q(counter_1_q), .clk(clock_1_out));  // open: load, D, count, carry, clr
  Clock clock_1 (.out(clock_1_out));
  Hex_Digit_Display hex_digit_display_1 (.value(counter_1_q[11:8]));  // open: dp
  LED isOdd (.in(alternatingBits[0]));
  Clock clock_2 (.out(clock_2_out));
  // Callout #(.background("#81e6df80"), .dx(26), .dy(-26), .foreground("#2e5c56"), .format("wrapped"), .text("use splitters to pull out one bit of a bus, or a subset of the bits of a bus"), .textwidth(219), .valign("top")) callout_9: pin names not known; wires that end beside it: clock_2_out, {callout_9_p2[7], alternatingBits[3], callout_9_p2[5], alternatingBits[2], bottomHalf[3], alternatingBits[1], bottomHalf[1], alternatingBits[0]}
  Hex_Digit_Display hex_digit_display_2 (.value(counter_1_q[7:4]));  // open: dp
  // Callout #(.background("#81e6df80"), .dx(-26), .dy(-15), .foreground("#2e5c56"), .format("wrapped"), .halign("center"), .text("split 12-bit bus into three 4-bit buses"), .textwidth(262), .valign("top")) callout_10: pin names not known; wires that end beside it: {callout_9_p2[7], alternatingBits[3], callout_9_p2[5], alternatingBits[2], bottomHalf[3], alternatingBits[1], bottomHalf[1], alternatingBits[0]}
  LED isNegative (.in(callout_9_p2[7]));
  Hex_Digit_Display hex_digit_display_3 (.value(counter_1_q[3:0]));  // open: dp

  assign {bottomHalf[2], bottomHalf[0]} = alternatingBits[1:0];
endmodule

module tunnel_examples (
  input  in_1
);

  wire and_1_out, bar, clock_1_out;
  wire [7:0] stored_value, switches;

  DipSwitch dipswitch_1 (
    .sw1(switches[7]), .sw2(switches[6]), .sw3(switches[5]), .sw4(switches[4]), .sw5(switches[3]),
    .sw6(switches[2]), .sw7(switches[1]), .sw8(switches[0]));
  Button button_1 (.out(bar));
  Hex_Digit_Display hex_digit_display_1 (.value(stored_value[7:4]));  // open: dp
  // Callout #(.background("#fcff3367"), .dx(-46), .dy(-21), .text("All tunnels\nnamed \"foo\"\nare invisibly\nconnected.")) callout_1: pin names not known
  // Callout #(.background("#89feff67"), .dx(-49), .dy(-42), .text("A tunnel can appear\nas many times as\nneeded. All three\n\"bar\" tunnels are\ninvisibly connected.")) callout_2: pin names not known
  Hex_Digit_Display hex_digit_display_2 (.value(stored_value[3:0]));  // open: dp
  // Callout #(.background("#bdbf2667"), .dx(72), .dy(-26), .halign("right"), .text("")) callout_3: pin names not known
  // Callout #(.background("#ff9dec67"), .dx(-46), .dy(-11), .text("Tunnels can\ncarry multi-bit\nsignals")) callout_4: pin names not known
  // Callout #(.background("#bfffae67"), .dx(-38), .format("wrapped"), .text("Like wires and splitters, tunnels have no \"direction\"... values are carried from any tunnel to every other identically-named tunnel."), .textwidth(184)) callout_5: pin names not known
  // Callout #(.background("#6bc7c767"), .dx(54), .dy(-36), .halign("right"), .text("")) callout_6: pin names not known
  // Callout #(.background("#6bc7c767"), .dx(50), .dy(56), .halign("right"), .text("")) callout_7: pin names not known
  and and_1 (and_1_out, in_1, bar);
  LED led_1 (.in(and_1_out));
  Register register_1 (.D(switches), .en(bar), .Q(stored_value), .clk(clock_1_out));  // open: clr
  Clock clock_1 (.out(clock_1_out));
  // Callout #(.background("#97c98967"), .dx(-17), .dy(-57), .format("wrapped"), .halign("right"), .text("Values go into this tunnel, and appear near the hex displays at left."), .textwidth(99), .valign("top")) callout_8: pin names not known

  // Other names for the same wires on the sheet: foo = in_1
endmodule

module clock_examples (
);

  wire clock_1_out, clock_2_out, clock_3_out, clock_4_out, clock_6_out, clock_7_out, clock_8_out, scope_1_p2;

  Clock #(.highDuration(20), .lowDuration(20)) clock_1 (.out(clock_1_out));
  // Scope #(.samples(128), .scopeheight(40), .scopewidth(160), .width(1)) scope_1: pin names not known; wires that end beside it: clock_1_out, scope_1_p2
  Clock #(.highDuration(60), .lowDuration(40)) clock_2 (.out(clock_2_out));
  // Scope #(.samples(128), .scopeheight(40), .scopewidth(160), .width(1)) scope_2: pin names not known; wires that end beside it: clock_2_out, scope_1_p2
  Clock #(.highDuration(20), .lowDuration(80)) clock_3 (.out(clock_3_out));
  // Scope #(.samples(128), .scopeheight(40), .scopewidth(160), .width(1)) scope_3: pin names not known; wires that end beside it: clock_3_out, scope_1_p2
  Clock #(.highDuration(20), .lowDuration(80), .phaseOffset(15)) clock_4 (.out(clock_4_out));
  // Scope #(.samples(128), .scopeheight(40), .scopewidth(160), .width(1)) scope_4: pin names not known; wires that end beside it: clock_4_out, scope_1_p2
  Clock clock_5 (.out(scope_1_p2));
  // Callout #(.background("#a8ff9573"), .dx(31), .dy(7), .format("wrapped"), .halign("right"), .text("Default clock: 1 tick high, 1 tick low."), .textwidth(136)) callout_1: pin names not known
  Clock #(.lowDuration(4)) clock_6 (.out(clock_6_out));
  // Callout #(.background("#ffb55073"), .dx(26), .dy(2), .format("wrapped"), .halign("right"), .text("Unbalanced clocks with 1 high for every 4 lows. The right one is phase-shifted by 1."), .textwidth(136)) callout_2: pin names not known
  LED led_1 (.in(clock_7_out));
  Clock clock_7 (.out(clock_7_out));
  Clock #(.lowDuration(4), .phaseOffset(1)) clock_8 (.out(clock_8_out));
  LED led_2 (.in(clock_6_out));
  LED led_3 (.in(clock_8_out));
  // Callout #(.background("#a8ff9573"), .dx(-15), .dy(-1), .format("wrapped"), .text("Balanced: 20 ticks high, 20 ticks low"), .textwidth(118)) callout_3: pin names not known
  // Callout #(.background("#a8ff9573"), .dx(-15), .dy(-1), .format("wrapped"), .text("60 high, 40 low"), .textwidth(118)) callout_4: pin names not known
  // Callout #(.background("#a8ff9573"), .dx(-15), .dy(-1), .format("wrapped"), .text("20 high, 80 low, no phase offset"), .textwidth(118)) callout_5: pin names not known
  // Callout #(.background("#a8ff9573"), .dx(-15), .dy(-1), .format("wrapped"), .text("20 high, 80 low, +15 phase offset"), .textwidth(118)) callout_6: pin names not known

  // Notes on the sheet:
  //   Poke any clock to make all clocks tick once. Or enable auto-ticks in the Simulate menu, and adjust the auto-tick frequency to your liking.
  //   All clocks in a simulation are internally tied to a common tick source.
  //   Let's visualize different clock parameters! For this demo, it's best to enable auto-ticks and set the auto-frequecy to around 32Hz. The scopes capture and display one value per clock cycle (2 ticks), so the clocks at the left are set to use 40 or more ticks per cycle.
  //   Notice how the +15 phase offset makes the high pulse arrive a little earlier (15 ticks earlier than the other display, above).
endmodule

module constant_examples (
  input  [1:0] select,
  output [15:0] out_2
);

  // Callout #(.background("#4324ff26"), .format("wrapped"), .text("A multiplexor, selecting one of four constants."), .textwidth(110)) callout_1: pin names not known
  // Callout #(.background("#ff00e626"), .dx(18), .dy(14), .format("wrapped"), .halign("right"), .text("Hex constants, 16 bits each (enough to fill a 4x4 LED Matrix)"), .textwidth(105)) callout_2: pin names not known
  Multiplexer #(.select(2), .width(16)) multiplexer_1 (
    .in0({16{1'b1}}), .in1({16{1'b1}}), .in2({16{1'b0}}), .in3({16{1'b0}}), .out(out_2), .sel(select));  // open: en
  DotMatrix #(.inputtype("row"), .matrixcols(4), .matrixrows(4)) dotmatrix_1 (
    .row0(out_2[3:0]), .row1(out_2[7:4]), .row2(out_2[11:8]), .row3(out_2[15:12]));
  // Callout #(.background("#4324ff26"), .format("wrapped"), .text("A multiplexor, selecting one of four constants."), .textwidth(110)) callout_3: pin names not known

  // Notes on the sheet:
  //   Use a constant when a circuit calls for a fixed, known value. It's a common mistake to use an Input Pin when a constant would be better:
  //   * Input Pin - takes on any value, depending on user interaction, and resets to zero when simulation is reset or project file is opened.
  //   * Constant - fixed value, does not change during a simulation, saved with project file.
endmodule
